# Fritzing sketch hci_gadgets_proj2 (saved by Fritzing 0.9.2b)
circuit board: 6.10246cm x 7.42179cm
breadboards: 1

parts:
  Battery = Battery block 9V
  IC1 = Voltage Regulator [package=78xxl]
  Y1 = Resonator [frequency="16 Mhz" package=THT]
  C3 = Capacitor [package=cap-pth-small2]
  R1 = Resistor [tolerance=±5% resistance=10k package=THT]
  AREF = male pin header, 1 pin [form="♂ (male)"]
  ICP = AVR ISP 6 Pin [package=2x3-ns]
  B-board_PW = female pin header, 2 pins [form="♀ (female)"]
  C4 = Capacitor [package=cap-pth-small2]
  C2 = Electrolytic Capacitor [capacitance=0.33µF package="100 mil [THT, electrolytic]"]
  Top = atmega328 [package=dip]
  Hdrs = male pin header, 20 pins [form="♂ (male)"]
  C1 = Electrolytic Capacitor [capacitance=0.1µF package="100 mil [THT, electrolytic]"]
  FTDI = male pin header, 6 pins [form="♂ (male)"]

nets:
  GND: Battery.-, IC1.GND, Y1.GND, C3.2, ICP.6, B-board_PW.pin2, C2.-, Top.GND, C1.-, FTDI.pin1, FTDI.pin2
  9V: Battery.+, IC1.IN, C2.+
  5V: IC1.OUT, C3.1, R1.Pin_0, ICP.2, B-board_PW.pin1, Top.VCC, Top.AVCC, C1.+, FTDI.pin3
  N1: Y1.0, Top.XLAT1
  N2: Y1.pin_1, Top.XLAT2
  reset: R1.Pin_1, ICP.5, C4.2, Top.RESET
  N3: AREF.pin1, Top.AREF
  D12: ICP.1, Top.D12, Hdrs.pin19
  D13: ICP.3, Top.D13, Hdrs.pin20
  D11: ICP.4, Top.D11_(PWM), Hdrs.pin18
  N4: C4.1, FTDI.pin6
  D0: Top.D0_(RX), Hdrs.pin7, FTDI.pin4
  D1: Top.D1_(TX), Hdrs.pin8, FTDI.pin5
  D2: Top.D2, Hdrs.pin9
  D3: Top.D3_(PWM), Hdrs.pin10
  D4: Top.D4, Hdrs.pin11
  D5: Top.D5_(PWM), Hdrs.pin12
  D6: Top.D6_(PWM), Hdrs.pin13
  D7: Top.D7, Hdrs.pin14
  D8: Top.D8, Hdrs.pin15
  D9: Top.D9_(PWM), Hdrs.pin16
  D10: Top.D10_(PWM), Hdrs.pin17
  A0: Top.A0, Hdrs.pin1
  A1: Top.A1, Hdrs.pin2
  A2: Top.A2, Hdrs.pin3
  A3: Top.A3, Hdrs.pin4
  A4: Top.A4, Hdrs.pin5
  A5: Top.A5, Hdrs.pin6

notes:
  Steven Connors
  D0
  D13
  A5
  A0
  P1 GND
  9V
  GND
  D12
  A4
  A3
  A2
  A1
  D1
  5V
  Human - Circuit Interaction
  D2
  D3
  D4
  D11
  D9
  D5
  D6
  D7
  D10
  D8
